// Logisim project homework..circ as structural Verilog: 1 circuit, main circuit main
module main (
  input  I0,
  input  I1,
  input  I2,
  input  I3,
  input  I4,
  input  I5,
  input  I6,
  input  I7
);

  wire nand_1_out, nand_2_out, nand_3_out, nand_4_out, nand_5_out, nand_6_out, nand_7_out, not_1_out,
       not_2_out, not_3_out, not_4_out, not_5_out, not_6_out, not_7_out;

  // NAND_Gate O0 has open pins: in0=nand_3_out, in1=nand_5_out, in2=nand_6_out, in3=nand_7_out, out=open
  nand nand_1 (nand_1_out, not_1_out, I1);
  not not_1 (not_1_out, I0);
  nand nand_2 (nand_2_out, not_1_out, not_2_out, I2);
  not not_2 (not_2_out, I1);
  not not_3 (not_3_out, I2);
  nand nand_3 (nand_3_out, not_1_out, not_2_out, not_3_out, not_4_out, I4);
  nand nand_4 (nand_4_out, not_1_out, not_2_out, not_3_out, I3);
  not not_4 (not_4_out, I3);
  // NAND_Gate O1 has open pins: in0=nand_2_out, in1=nand_4_out, in2=nand_6_out, in3=nand_7_out, out=open
  nand nand_5 (nand_5_out, not_1_out, not_2_out, not_3_out, not_4_out, not_5_out, I5);
  not not_5 (not_5_out, I4);
  not not_6 (not_6_out, I5);
  // NAND_Gate O2 has open pins: in0=nand_1_out, in1=nand_4_out, in2=nand_5_out, in3=nand_7_out, out=open
  nand nand_6 (nand_6_out, not_1_out, not_2_out, not_3_out, not_4_out, not_5_out, not_6_out, I6);
  not not_7 (not_7_out, I6);
  nand nand_7 (nand_7_out, not_1_out, not_2_out, not_3_out, not_4_out, not_5_out, not_6_out, not_7_out, I7);
endmodule
