// Logisim project lab3.5.circ as structural Verilog: 1 circuit, main circuit main
module main (
  input  CLK,
  input  LD,
  input  [3:0] HH1,
  input  [3:0] HH0,
  input  [3:0] MM1,
  input  [3:0] MM0,
  input  [3:0] SS1,
  input  [3:0] SS0,
  output [3:0] HH_H,
  output [3:0] HH_L,
  output [3:0] MM_H,
  output [3:0] MM_L,
  output [3:0] out_13,
  output [3:0] SS_H,
  output [3:0] SS_L,
  output LED_R,
  output LED_G,
  output LED_B,
  output INErr
);

  wire \_0点 , and_1_out, and_2_out, and_3_out, and_4_out, and_5_out, and_6_out, comparator_1_eq,
       comparator_2_eq, comparator_3_eq, comparator_4_eq, comparator_4_gt, comparator_5_eq, comparator_5_gt,
       comparator_6_eq, comparator_6_gt, comparator_7_eq, comparator_7_gt, comparator_8_eq, comparator_8_gt,
       comparator_9_eq, comparator_9_gt, comparator_10_eq, comparator_11_eq, comparator_12_eq,
       comparator_13_gt, comparator_14_eq, comparator_16_eq, comparator_17_eq, LED_EN, or_1_out, or_2_out,
       or_3_out, START, STOP;

  and and_1 (and_1_out, LD, ~INErr);  // AND_Gate
  Comparator #(.width(4), .mode("unsigned")) comparator_1 (
    .a(4'b1001), .b(HH_L), .eq(comparator_1_eq));  // open: gt, lt
  Comparator #(.width(4), .mode("unsigned")) comparator_2 (
    .a(4'b1001), .b(MM_L), .eq(comparator_2_eq));  // open: gt, lt
  and and_2 (and_2_out, comparator_1_eq, and_4_out);
  and and_3 (and_3_out, comparator_2_eq, and_5_out);
  Comparator #(.width(4), .mode("unsigned")) comparator_3 (
    .a(4'b1001), .b(SS_L), .eq(comparator_3_eq));  // open: gt, lt
  Hex_Digit_Display hex_digit_display_1 (.value(HH_H));  // open: dp
  CNTR4U cntr4u_1 (
    .CLK(CLK), .LD(and_1_out), .CLR(\_0点 ), .Q0(HH_H[0]), .Q1(HH_H[1]), .D0(HH1[0]), .D1(HH1[1]),
    .D2(HH1[2]), .Q2(HH_H[2]), .Q3(HH_H[3]), .D3(HH1[3]), .ENP(and_2_out), .ENT(and_2_out));  // open: RCO
  CNTR4U cntr4u_2 (
    .CLK(CLK), .LD(and_1_out), .CLR(and_4_out), .Q0(MM_H[0]), .Q1(MM_H[1]), .D0(MM1[0]), .D1(MM1[1]),
    .D2(MM1[2]), .Q2(MM_H[2]), .Q3(MM_H[3]), .D3(MM1[3]), .ENP(and_3_out), .ENT(and_3_out));  // open: RCO
  CNTR4U cntr4u_3 (
    .CLK(CLK), .LD(and_1_out), .CLR(and_5_out), .Q0(SS_H[0]), .Q1(SS_H[1]), .D0(SS1[0]), .D1(SS1[1]),
    .D2(SS1[2]), .Q2(SS_H[2]), .Q3(SS_H[3]), .D3(SS1[3]), .ENP(comparator_3_eq), .ENT(comparator_3_eq));  // open: RCO
  Comparator #(.width(4), .mode("unsigned")) comparator_4 (
    .a(HH1), .b(4'b0011), .gt(comparator_4_gt), .eq(comparator_4_eq));  // open: lt
  Comparator #(.width(4), .mode("unsigned")) comparator_5 (
    .a(HH0), .b(4'b1010), .gt(comparator_5_gt), .eq(comparator_5_eq));  // open: lt
  Comparator #(.width(4), .mode("unsigned")) comparator_6 (
    .a(MM1), .b(4'b0110), .gt(comparator_6_gt), .eq(comparator_6_eq));  // open: lt
  Comparator #(.width(4), .mode("unsigned")) comparator_7 (
    .a(MM0), .b(4'b1010), .gt(comparator_7_gt), .eq(comparator_7_eq));  // open: lt
  Comparator #(.width(4), .mode("unsigned")) comparator_8 (
    .a(SS1), .b(4'b0110), .gt(comparator_8_gt), .eq(comparator_8_eq));  // open: lt
  Comparator #(.width(4), .mode("unsigned")) comparator_9 (
    .a(SS0), .b(4'b1010), .gt(comparator_9_gt), .eq(comparator_9_eq));  // open: lt
  Hex_Digit_Display hex_digit_display_2 (.value(HH_L), .dp(1'b1));
  Hex_Digit_Display hex_digit_display_3 (.value(MM_H));  // open: dp
  CNTR4U cntr4u_4 (
    .CLK(CLK), .LD(LED_EN), .CLR(STOP), .Q0(out_13[0]), .Q1(out_13[1]), .D0(1'b1), .D1(1'b0), .D2(1'b0),
    .Q2(out_13[2]), .Q3(out_13[3]), .D3(1'b0), .ENP(START), .ENT(START));  // open: RCO
  Hex_Digit_Display hex_digit_display_4 (.value(MM_L), .dp(1'b1));
  Hex_Digit_Display hex_digit_display_5 (.value(SS_H));  // open: dp
  or or_1 (or_1_out, \_0点 , and_2_out);
  Comparator #(.width(4), .mode("unsigned")) comparator_10 (
    .a(4'b0101), .b(MM_H), .eq(comparator_10_eq));  // open: gt, lt
  Comparator #(.width(4), .mode("unsigned")) comparator_11 (
    .a(4'b0101), .b(SS_H), .eq(comparator_11_eq));  // open: gt, lt
  or or_2 (or_2_out, comparator_4_gt, comparator_4_eq, comparator_5_gt, comparator_5_eq, comparator_6_gt, comparator_6_eq, comparator_7_gt, comparator_7_eq, comparator_8_gt, comparator_8_eq, comparator_9_gt, comparator_9_eq);
  Hex_Digit_Display hex_digit_display_6 (.value(SS_L), .dp(1'b1));
  and and_4 (and_4_out, comparator_10_eq, and_3_out);
  and and_5 (and_5_out, comparator_11_eq, comparator_3_eq);
  Comparator #(.width(4), .mode("unsigned")) comparator_12 (
    .a(HH1), .b(4'b0010), .eq(comparator_12_eq));  // open: gt, lt
  Comparator #(.width(4), .mode("unsigned")) comparator_13 (
    .a(HH0), .b(4'b0011), .gt(comparator_13_gt));  // open: eq, lt
  Comparator #(.width(4), .mode("unsigned")) comparator_14 (
    .a(4'b0000), .b(out_13), .eq(comparator_14_eq));  // open: gt, lt
  Comparator #(.width(4), .mode("unsigned")) comparator_15 (.a(out_13), .b(4'b1010), .eq(STOP));  // open: gt, lt
  xor xor_1 (LED_R, out_13[0], out_13[1]);
  xor xor_2 (LED_G, out_13[1], out_13[2]);
  xor xor_3 (LED_B, out_13[2], 1'b0);
  CNTR4U cntr4u_5 (
    .CLK(CLK), .LD(and_1_out), .CLR(or_1_out), .Q0(HH_L[0]), .Q1(HH_L[1]), .D0(HH0[0]), .D1(HH0[1]),
    .D2(HH0[2]), .Q2(HH_L[2]), .Q3(HH_L[3]), .D3(HH0[3]), .ENP(and_4_out), .ENT(and_4_out));  // open: RCO
  CNTR4U cntr4u_6 (
    .CLK(CLK), .LD(and_1_out), .CLR(and_3_out), .Q0(MM_L[0]), .Q1(MM_L[1]), .D0(MM0[0]), .D1(MM0[1]),
    .D2(MM0[2]), .Q2(MM_L[2]), .Q3(MM_L[3]), .D3(MM0[3]), .ENP(and_5_out), .ENT(and_5_out));  // open: RCO
  CNTR4U cntr4u_7 (
    .CLK(CLK), .LD(and_1_out), .CLR(comparator_3_eq), .Q0(SS_L[0]), .Q1(SS_L[1]), .D0(SS0[0]), .D1(SS0[1]),
    .D2(SS0[2]), .Q2(SS_L[2]), .Q3(SS_L[3]), .D3(SS0[3]), .ENP(1'b1), .ENT(1'b1));  // open: RCO
  and and_6 (and_6_out, comparator_12_eq, comparator_13_gt);
  not not_1 (START, comparator_14_eq);
  or or_3 (or_3_out, and_6_out, or_2_out);
  and and_7 (INErr, or_3_out, LD);
  // RGBLed RGBLED: pin names not known; wires that end beside it: LED_R, LED_G, LED_B
  Comparator #(.width(4), .mode("unsigned")) comparator_16 (
    .a(HH_H), .b(4'b0010), .eq(comparator_16_eq));  // open: gt, lt
  Comparator #(.width(4), .mode("unsigned")) comparator_17 (
    .a(HH_L), .b(4'b0011), .eq(comparator_17_eq));  // open: gt, lt
  Comparator #(.width(16), .mode("unsigned")) comparator_18 (
    .a({MM_H, MM_L, SS_H, SS_L}), .b(16'h5959), .eq(LED_EN));  // open: gt, lt
  and and_8 (\_0点 , comparator_16_eq, comparator_17_eq, and_4_out);

  // Other names for the same wires on the sheet: S0[3:0] = SS_L; S1[3:0] = SS_H; M0[3:0] = MM_L; M1[3:0] = MM_H;
  //   H0[3:0] = HH_L; H1[3:0] = HH_H; LED[3:0] = out_13

  // Notes on the sheet:
  //   设置初始时间BCD码
  //   输入信号
  //   请勿修改引脚名称、电路名称及电路封装外观
  //   数字时钟
  //   提示：使用4位二进制加法计数器子电路、比较器和独立逻辑门组件实现数字时钟。
  //   在载入有效时，检测设置数据错误
  //   生成三色LED显示信号，持续10个时钟周期
endmodule
