// Logisim project 32位无符号乘法.circ as structural Verilog: 8 circuits, main circuit main
// 1
module main (
  input  CLK,
  input  [3:0] X,
  input  [3:0] Y,
  input  Reset,
  output [7:0] Prod
);

  wire clock_1_out, LOAD, not_1_out, STOP, \加减器_1_cout ;
  wire [3:0] \_4位同步计数器_q0 , multiplexer_1_out, multiplexer_2_out, multiplexer_2_out_2, \加减器_1_f ;
  wire [7:0] \桶形移位器_dataout ;

  Clock clock_1 (.out(clock_1_out));
  not not_1 (not_1_out, STOP);
  Multiplexer #(.width(4), .enable("false")) multiplexer_1 (
    .in0(4'b0000), .in1(X), .out(multiplexer_1_out), .sel(Prod[0]));
  Hex_Digit_Display hex_digit_display_1 (.value(X));  // open: dp
  \加减器  \u_加减器_1  (.X(multiplexer_1_out), .F(\加减器_1_f ), .Cout(\加减器_1_cout ), .Cin(1'b0), .Y(Prod[7:4]));
  Hex_Digit_Display hex_digit_display_2 (.value(Y));  // open: dp
  Register #(.width(4), .Select("low")) register_1 (
    .D(multiplexer_2_out_2), .en(not_1_out), .Q(Prod[7:4]), .clk(CLK), .clr(Reset));
  Hex_Digit_Display hex_digit_display_3 (.value(Prod[7:4]));  // open: dp
  // Probe on nothing
  \桶形移位器  \u_桶形移位器  (
    .DataIn({\加减器_1_f , Prod[3:0]}), .shamt(3'b001), .L_R(1'b0), .A_L(1'b0), .DataOut(\桶形移位器_dataout ),
    .IN(\加减器_1_cout ));
  Hex_Digit_Display hex_digit_display_4 (.value(Prod[3:0]));  // open: dp
  // Probe on nothing
  Register #(.width(4), .Select("low")) Y_2 (
    .D(multiplexer_2_out), .en(not_1_out), .Q(Prod[3:0]), .clk(CLK), .clr(Reset));
  Multiplexer #(.width(8), .enable("false")) multiplexer_2 (
    .in0(\桶形移位器_dataout ), .in1({4'b0000, Y}), .out({multiplexer_2_out_2, multiplexer_2_out}), .sel(LOAD));
  // Probe on X
  // Probe on Y
  // Probe on Prod
  Comparator #(.width(4)) comparator_1 (.a(\_4位同步计数器_q0 ), .b(4'b0000), .eq(LOAD));  // open: gt, lt
  Comparator #(.width(4)) comparator_2 (.a(\_4位同步计数器_q0 ), .b(4'b0101), .eq(STOP));  // open: gt, lt
  \同步计数器  \_4位同步计数器  (
    .CLK(CLK), .LD(1'b0), .CLR(Reset), .Q0(\_4位同步计数器_q0 [0]), .Q1(\_4位同步计数器_q0 [1]), .D0(1'b0), .D1(1'b0),
    .D2(1'b0), .Q2(\_4位同步计数器_q0 [2]), .Q3(\_4位同步计数器_q0 [3]), .D3(1'b0), .ENP(not_1_out), .ENT(not_1_out));  // open: RCO

  // Other names for the same wires on the sheet: RST = Reset; Z[7:0] = Prod

  // Notes on the sheet:
  //   X
  //   输入引脚
  //   P
  //   =
  //   请勿修改引脚名称、电路名称及电路封装外观
  //   提示: 采用无符号数一位乘法实现4位二进制乘法器，禁止直接使用乘法器组件
  //   ×
  //   =
  //   输出引脚
endmodule

module \同步计数器  (
  input  CLK,
  input  LD,
  input  CLR,
  input  D0,
  input  D1,
  input  D2,
  input  D3,
  input  ENP,
  input  ENT,
  output Q0,
  output Q1,
  output Q2,
  output Q3,
  output RCO
);

  wire and_1_out, and_2_out, and_3_out, and_4_out, and_5_out, and_6_out, and_7_out, and_8_out, and_9_out,
       and_10_out, and_11_out, and_12_out, and_13_out, and_14_out, d_ff_1_qn, d_ff_2_qn, d_ff_3_qn,
       d_ff_4_qn, nor_1_out, nor_2_out, not_1_out, not_2_out, not_3_out, or_1_out, or_2_out, or_3_out,
       or_4_out, xor_1_out, xor_2_out, xor_3_out, xor_4_out;

  not not_1 (not_1_out, CLK);
  not not_2 (not_2_out, d_ff_1_qn);
  nor nor_1 (nor_1_out, d_ff_2_qn, d_ff_1_qn);
  nor nor_2 (nor_2_out, d_ff_3_qn, d_ff_2_qn, d_ff_1_qn);
  and and_1 (and_1_out, LD, ~CLR);  // AND_Gate
  and and_2 (and_2_out, ~and_1_out, ~CLR);  // AND_Gate
  and and_3 (and_3_out, not_2_out, and_6_out);
  and and_4 (and_4_out, nor_1_out, and_6_out);
  and and_5 (and_5_out, nor_2_out, and_6_out);
  and and_6 (and_6_out, ENP, ENT);
  xor xor_1 (xor_1_out, and_6_out, ~d_ff_1_qn);  // XOR_Gate
  xor xor_2 (xor_2_out, and_3_out, ~d_ff_2_qn);  // XOR_Gate
  xor xor_3 (xor_3_out, and_4_out, ~d_ff_3_qn);  // XOR_Gate
  xor xor_4 (xor_4_out, and_5_out, ~d_ff_4_qn);  // XOR_Gate
  not not_3 (not_3_out, ENT);
  and and_7 (and_7_out, and_1_out, D0);
  and and_8 (and_8_out, and_2_out, xor_1_out);
  and and_9 (and_9_out, and_1_out, D1);
  and and_10 (and_10_out, and_2_out, xor_2_out);
  and and_11 (and_11_out, and_1_out, D2);
  and and_12 (and_12_out, and_2_out, xor_3_out);
  and and_13 (and_13_out, and_1_out, D3);
  and and_14 (and_14_out, and_2_out, xor_4_out);
  nor nor_3 (RCO, d_ff_4_qn, d_ff_3_qn, d_ff_2_qn, d_ff_1_qn, not_3_out);
  or or_1 (or_1_out, and_7_out, and_8_out);
  or or_2 (or_2_out, and_9_out, and_10_out);
  or or_3 (or_3_out, and_11_out, and_12_out);
  or or_4 (or_4_out, and_13_out, and_14_out);
  D_Flip_Flop #(.trigger("falling")) d_ff_1 (
    .clk(not_1_out), .D(or_1_out), .Q(Q0), .Qn(d_ff_1_qn));  // open: preset, reset
  D_Flip_Flop #(.trigger("falling")) d_ff_2 (
    .clk(not_1_out), .D(or_2_out), .Q(Q1), .Qn(d_ff_2_qn));  // open: preset, reset
  D_Flip_Flop #(.trigger("falling")) d_ff_3 (
    .clk(not_1_out), .D(or_3_out), .Q(Q2), .Qn(d_ff_3_qn));  // open: preset, reset
  D_Flip_Flop #(.trigger("falling")) d_ff_4 (
    .clk(not_1_out), .D(or_4_out), .Q(Q3), .Qn(d_ff_4_qn));  // open: preset, reset

  // Notes on the sheet:
  //   输入引脚
  //   请勿修改引脚名称、电路名称及电路封装外观
  //   提示：使用独立逻辑门实现4位二进制同步计数器，禁止直接使用计数器组件。
  //   输出引脚
endmodule

module \加减器  (
  input  [3:0] X,
  input  [3:0] Y,
  input  Cin,
  output [3:0] F,
  output Cout
);

  wire fa_1_cout, fa_2_cout, fa_3_cout;
  wire [3:0] bit_extender_1_out, xor_1_out;

  assign bit_extender_1_out = {{3{Cin}}, Cin};  // Bit_Extender bit_extender_1
  Hex_Digit_Display hex_digit_display_1 (.value(X), .dp(1'b0));
  assign xor_1_out = bit_extender_1_out ^ Y;  // XOR_Gate xor_1, 4 bits wide
  Hex_Digit_Display hex_digit_display_2 (.value(xor_1_out), .dp(1'b0));
  FA fa_1 (.A(X[0]), .B(xor_1_out[0]), .Cin(Cin), .F(F[0]), .Cout(fa_1_cout));
  Hex_Digit_Display hex_digit_display_3 (.value(F), .dp(1'b0));
  FA fa_2 (.A(X[1]), .B(xor_1_out[1]), .Cin(fa_1_cout), .F(F[1]), .Cout(fa_2_cout));
  FA fa_3 (.A(X[2]), .B(xor_1_out[2]), .Cin(fa_2_cout), .F(F[2]), .Cout(fa_3_cout));
  FA fa_4 (.A(X[3]), .B(xor_1_out[3]), .Cin(fa_3_cout), .F(F[3]), .Cout(Cout));

  // Other names for the same wires on the sheet: SUM[3:0] = F; 操作数x[3:0] = X; 操作数y[3:0] = Y

  // Notes on the sheet:
  //   输入引脚
  //   +
  //   =
  //   请勿修改引脚名称、电路名称及电路封装外观
  //   提示：使用独立逻辑门及全加器FA子电路实现4位二进制数加减法器，禁止直接使用加减法器组件。
  //   输出引脚
endmodule

module FA (
  input  A,
  input  B,
  input  Cin,
  output F,
  output Cout
);

  wire and_1_out, and_2_out, and_3_out;

  xor xor_1 (F, A, B, Cin);
  and and_1 (and_1_out, A, B);
  and and_2 (and_2_out, B, Cin);
  and and_3 (and_3_out, A, Cin);
  or or_1 (Cout, and_1_out, and_2_out, and_3_out);

  // Notes on the sheet:
  //   全加器
endmodule

module \桶形移位器  (
  input  [7:0] DataIn,
  input  [2:0] shamt,
  input  IN,
  input  L_R,
  input  A_L,
  output [7:0] DataOut
);

  wire [7:0] multiplexer_1_out, multiplexer_2_out, multiplexer_3_out, multiplexer_4_out, multiplexer_5_out;

  Multiplexer #(.width(8), .enable("false")) multiplexer_1 (
    .in0(DataIn), .in1(multiplexer_2_out), .out(multiplexer_1_out), .sel(shamt[0]));
  Multiplexer #(.select(2), .width(8), .enable("false")) multiplexer_2 (
    .in0({IN, DataIn[7:1]}), .in1({{2{DataIn[7]}}, DataIn[6:1]}), .in2({DataIn[6:0], 1'b0}),
    .in3({DataIn[6:0], DataIn[7]}), .out(multiplexer_2_out), .sel({L_R, A_L}));
  Multiplexer #(.select(2), .width(8), .enable("false")) multiplexer_3 (
    .in0({2'b00, multiplexer_1_out[7:2]}), .in1({{3{multiplexer_1_out[7]}}, multiplexer_1_out[6:2]}),
    .in2({multiplexer_1_out[5:0], 2'b00}), .in3({multiplexer_1_out[5:0], multiplexer_1_out[7:6]}),
    .out(multiplexer_3_out), .sel({L_R, A_L}));
  Multiplexer #(.width(8), .enable("false")) multiplexer_4 (
    .in0(multiplexer_1_out), .in1(multiplexer_3_out), .out(multiplexer_4_out), .sel(shamt[1]));
  Multiplexer #(.select(2), .width(8), .enable("false")) multiplexer_5 (
    .in0({4'b0000, multiplexer_4_out[7:4]}), .in1({{5{multiplexer_4_out[7]}}, multiplexer_4_out[6:4]}),
    .in2({multiplexer_4_out[3:0], 4'b0000}), .in3({multiplexer_4_out[3:0], multiplexer_4_out[7:4]}),
    .out(multiplexer_5_out), .sel({L_R, A_L}));
  Multiplexer #(.width(8), .enable("false")) multiplexer_6 (
    .in0(multiplexer_4_out), .in1(multiplexer_5_out), .out(DataOut), .sel(shamt[2]));

  // Other names for the same wires on the sheet: Input = IN; Din[7:0] = DataIn; Arth_Logic = A_L; Left_Right = L_R;
  //   Dout[7:0] = DataOut

  // Notes on the sheet:
  //   L/R,A/L: 00逻辑右移，01算术右移，10逻辑左移，11：循环左移
  //   输入引脚
  //   请勿修改引脚名称、电路名称及电路封装外观
  //   提示：使用多路选择器级联实现8位桶形移位器，禁止直接使用移位器组件。
  //   输出引脚
endmodule

module \_8位无符号乘法  (
  input  CLK,
  input  ReSet,
  input  [7:0] X,
  input  [7:0] Y,
  output [15:0] out_5
);

  wire [7:0] main_1_prod, main_2_prod, main_3_prod, main_4_prod;
  wire [15:0] adder_1_out, adder_2_out, bit_extender_1_out, bit_extender_2_out, bit_extender_3_out,
       bit_extender_4_out, shifter_1_out, shifter_2_out, shifter_3_out;

  // Probe on X[3:0]
  // Probe on X
  // Probe on Y
  // Probe on X[7:4]
  // Probe on Y[3:0]
  // Probe on Y[7:4]
  main main_1 (.CLK(CLK), .X(X[3:0]), .Y(Y[3:0]), .Prod(main_1_prod), .Reset(ReSet));
  // Probe on main_1_prod
  main main_2 (.CLK(CLK), .X(X[7:4]), .Y(Y[3:0]), .Prod(main_2_prod), .Reset(ReSet));
  // Probe on main_2_prod
  main main_3 (.CLK(CLK), .X(X[3:0]), .Y(Y[7:4]), .Prod(main_3_prod), .Reset(ReSet));
  // Probe on main_3_prod
  main main_4 (.CLK(CLK), .X(X[7:4]), .Y(Y[7:4]), .Prod(main_4_prod), .Reset(ReSet));
  assign bit_extender_1_out = {{8{1'b0}}, main_1_prod};  // Bit_Extender bit_extender_1
  assign bit_extender_2_out = {{8{1'b0}}, main_2_prod};  // Bit_Extender bit_extender_2
  assign bit_extender_3_out = {{8{1'b0}}, main_3_prod};  // Bit_Extender bit_extender_3
  assign bit_extender_4_out = {{8{1'b0}}, main_4_prod};  // Bit_Extender bit_extender_4
  // Probe on main_4_prod
  Shifter #(.width(16)) shifter_1 (.in(bit_extender_2_out), .\dist (4'b0100), .out(shifter_1_out));
  Shifter #(.width(16)) shifter_2 (.in(bit_extender_3_out), .\dist (4'b0100), .out(shifter_2_out));
  Shifter #(.width(16)) shifter_3 (.in(bit_extender_4_out), .\dist (4'b1000), .out(shifter_3_out));
  // Probe on bit_extender_1_out
  // Probe on shifter_1_out
  // Probe on shifter_2_out
  // Probe on shifter_3_out
  Adder #(.width(16)) adder_1 (.a(bit_extender_1_out), .b(shifter_1_out), .out(adder_1_out));  // open: cin, cout
  Adder #(.width(16)) adder_2 (.a(adder_1_out), .b(shifter_2_out), .out(adder_2_out));  // open: cin, cout
  // Probe on out_5
  Adder #(.width(16)) adder_3 (.a(adder_2_out), .b(shifter_3_out), .out(out_5));  // open: cin, cout
endmodule

module \_16位无符号乘法  (
  input  CLK,
  input  ReSet,
  input  [15:0] X,
  input  [15:0] Y,
  output [31:0] out_5
);

  wire [15:0] \_8位无符号乘法器_2_out_5 , \_8位无符号乘法器_3_out_5 , \_8位无符号乘法器_4_out_5 , \_8位无符号乘法器_out_5 ;
  wire [31:0] adder_1_out, adder_2_out, bit_extender_1_out, bit_extender_2_out, bit_extender_3_out,
       bit_extender_4_out, shifter_1_out, shifter_2_out, shifter_3_out;

  // Probe on X
  // Probe on Y
  \_8位无符号乘法  \_8位无符号乘法器  (.CLK(CLK), .ReSet(ReSet), .X(X[7:0]), .Y(Y[7:0]), .out_5(\_8位无符号乘法器_out_5 ));
  \_8位无符号乘法  \_8位无符号乘法器_2  (.CLK(CLK), .ReSet(ReSet), .X(Y[7:0]), .Y(X[15:8]), .out_5(\_8位无符号乘法器_2_out_5 ));
  \_8位无符号乘法  \_8位无符号乘法器_3  (.CLK(CLK), .ReSet(ReSet), .X(X[7:0]), .Y(Y[15:8]), .out_5(\_8位无符号乘法器_3_out_5 ));
  \_8位无符号乘法  \_8位无符号乘法器_4  (.CLK(CLK), .ReSet(ReSet), .X(X[15:8]), .Y(Y[15:8]), .out_5(\_8位无符号乘法器_4_out_5 ));
  // Probe on \_8位无符号乘法器_out_5 
  // Probe on \_8位无符号乘法器_2_out_5 
  // Probe on \_8位无符号乘法器_3_out_5 
  // Probe on \_8位无符号乘法器_4_out_5 
  // Probe on bit_extender_1_out
  assign bit_extender_1_out = {{16{1'b0}}, \_8位无符号乘法器_out_5 };  // Bit_Extender bit_extender_1
  assign bit_extender_2_out = {{16{1'b0}}, \_8位无符号乘法器_2_out_5 };  // Bit_Extender bit_extender_2
  Shifter #(.width(32)) shifter_1 (.in(bit_extender_2_out), .\dist (5'b01000), .out(shifter_1_out));
  assign bit_extender_3_out = {{16{1'b0}}, \_8位无符号乘法器_3_out_5 };  // Bit_Extender bit_extender_3
  Shifter #(.width(32)) shifter_2 (.in(bit_extender_3_out), .\dist (5'b01000), .out(shifter_2_out));
  assign bit_extender_4_out = {{16{1'b0}}, \_8位无符号乘法器_4_out_5 };  // Bit_Extender bit_extender_4
  Shifter #(.width(32)) shifter_3 (.in(bit_extender_4_out), .\dist (5'b10000), .out(shifter_3_out));
  // Probe on shifter_1_out
  // Probe on shifter_2_out
  // Probe on shifter_3_out
  Adder #(.width(32)) adder_1 (.a(bit_extender_1_out), .b(shifter_1_out), .out(adder_1_out));  // open: cin, cout
  Adder #(.width(32)) adder_2 (.a(adder_1_out), .b(shifter_2_out), .out(adder_2_out));  // open: cin, cout
  // Probe on out_5
  Adder #(.width(32)) adder_3 (.a(adder_2_out), .b(shifter_3_out), .out(out_5));  // open: cin, cout
endmodule

module \_32位无符号乘法  (
  input  [31:0] X,
  input  [31:0] Y,
  input  ReSet,
  output [31:0] out_4
);

  wire clock_1_out;
  wire [31:0] adder_1_out, \n16位无符号乘法_1_out_5 , \n16位无符号乘法_2_out_5 , \n16位无符号乘法_3_out_5 , shifter_1_out,
       shifter_2_out;

  Clock clock_1 (.out(clock_1_out));
  // Probe on X
  // Probe on X[15:0]
  // Probe on X[31:16]
  // Probe on Y[15:0]
  // Probe on Y[31:16]
  // Probe on Y
  \_16位无符号乘法  \u_16位无符号乘法_1  (.CLK(clock_1_out), .ReSet(ReSet), .X(X[15:0]), .Y(Y[15:0]), .out_5(\n16位无符号乘法_1_out_5 ));
  // Probe on \n16位无符号乘法_1_out_5 
  \_16位无符号乘法  \u_16位无符号乘法_2  (.CLK(clock_1_out), .ReSet(ReSet), .X(Y[15:0]), .Y(X[31:16]), .out_5(\n16位无符号乘法_2_out_5 ));
  // Probe on \n16位无符号乘法_2_out_5 
  \_16位无符号乘法  \u_16位无符号乘法_3  (.CLK(clock_1_out), .ReSet(ReSet), .X(X[15:0]), .Y(Y[31:16]), .out_5(\n16位无符号乘法_3_out_5 ));
  // Probe on \n16位无符号乘法_3_out_5 
  // Probe on out_4
  // Probe on \n16位无符号乘法_1_out_5 
  Shifter #(.width(32)) shifter_1 (.in(\n16位无符号乘法_2_out_5 ), .\dist (5'b10000), .out(shifter_1_out));
  // Probe on shifter_1_out
  // Probe on shifter_2_out
  Shifter #(.width(32)) shifter_2 (.in(\n16位无符号乘法_3_out_5 ), .\dist (5'b10000), .out(shifter_2_out));
  Adder #(.width(32)) adder_1 (.a(\n16位无符号乘法_1_out_5 ), .b(shifter_1_out), .out(adder_1_out));  // open: cin, cout
  Adder #(.width(32)) adder_2 (.a(adder_1_out), .b(shifter_2_out), .out(out_4));  // open: cin, cout
  // Probe on out_4

  // Other names for the same wires on the sheet: F[31:0] = out_4

  // Notes on the sheet:
  //   X
endmodule
