// Logisim project 32位无符号除法.circ as structural Verilog: 1 circuit, main circuit main
module main (
  input  [31:0] in_1,
  input  XSF,
  input  [31:0] in_3,
  input  XSF_2,
  input  RESET,
  output [31:0] \商 ,
  output [31:0] out_7
);

  wire _1, _2, clock_1_out, comparator_1_eq, comparator_1_gt, comparator_2_eq, comparator_2_lt, not_1_out,
       not_2_out;
  wire [0:0] or_1_out;
  wire [5:0] counter_1_q;
  wire [31:0] multiplexer_1_out, multiplexer_2_out, subtractor_1_out;

  Clock clock_1 (.out(clock_1_out));
  Register #(.width(32), .Select("high")) Q (
    .D(multiplexer_1_out), .en(not_1_out), .Q(out_7), .clk(clock_1_out), .clr(RESET));
  not not_1 (not_1_out, _2);
  // Probe on in_1
  // Probe on in_3
  // Probe on out_7
  // Probe on out_7
  Comparator #(.width(32), .mode("unsigned")) comparator_1 (
    .a({out_7[30:0], \商 [31]}), .b(in_3), .gt(comparator_1_gt), .eq(comparator_1_eq));  // open: lt
  or or_1 (or_1_out[0], comparator_1_gt, comparator_1_eq);
  Subtractor #(.width(32)) subtractor_1 (
    .a({out_7[30:0], \商 [31]}), .b(in_3), .out(subtractor_1_out));  // open: bin, bout
  // Probe on \商 
  // Probe on out_7
  // Probe on {out_7[30:0], \商 [31]}
  Multiplexer #(.width(32), .enable("false")) multiplexer_1 (
    .in0({out_7[30:0], \商 [31]}), .in1(subtractor_1_out), .out(multiplexer_1_out), .sel(or_1_out[0]));
  Multiplexer #(.width(32), .enable("false")) multiplexer_2 (
    .in0(in_1), .in1({\商 [30:0], or_1_out[0]}), .out(multiplexer_2_out), .sel(_1));
  Counter #(.width(6), .max('h3f), .ongoal("stay")) counter_1 (
    .D({6{1'b0}}), .Q(counter_1_q), .clk(clock_1_out), .clr(RESET));  // open: load, count, carry, preset, down
  Comparator #(.width(6), .mode("unsigned")) comparator_2 (
    .a(6'b000001), .b(counter_1_q), .eq(comparator_2_eq), .lt(comparator_2_lt));  // open: gt
  Comparator #(.width(6), .mode("unsigned")) comparator_3 (.a(6'b100000), .b(counter_1_q), .lt(_2));  // open: gt, eq
  // Probe on \商 
  Register #(.width(32), .Select("high")) R (
    .D(multiplexer_2_out), .en(not_2_out), .Q(\商 ), .clk(clock_1_out), .clr(RESET));
  not not_2 (not_2_out, _2);
  // Probe on \商 
  or or_2 (_1, comparator_2_eq, comparator_2_lt);

  assign XSF_2 = XSF;

  // Other names for the same wires on the sheet: 余数[31:0] = out_7; X[31:0] = in_1; Y[31:0] = in_3
endmodule
