// Logisim project lab4.2.circ as structural Verilog: 1 circuit, main circuit main
// 16-CLA
module main (
  input  C0,
  input  [15:0] X,
  input  [15:0] Y,
  output C16,
  output Pg,
  output Gg,
  output [15:0] S
);

  wire clu4_1_c1, clu4_1_c2, clu4_1_c3, main_1_gg, main_1_pg, main_2_gg, main_2_pg, main_3_gg, main_3_pg,
       main_4_gg, main_4_pg;

  lab4_1_main main_1 (
    .X(X[15:12]), .F(S[15:12]), .Cout(C16), .Y(Y[15:12]), .Pg(main_1_pg), .Cin(clu4_1_c3), .Gg(main_1_gg));
  CLU4 clu4_1 (
    .P0(main_4_pg), .P1(main_3_pg), .P2(main_2_pg), .P3(main_1_pg), .C1(clu4_1_c1), .C3(clu4_1_c3),
    .G0(main_4_gg), .G1(main_3_gg), .G2(main_2_gg), .G3(main_1_gg), .C2(clu4_1_c2), .C0(C0), .Pg(Pg), .Gg(Gg));  // open: C4
  lab4_1_main main_2 (
    .X(X[11:8]), .F(S[11:8]), .Y(Y[11:8]), .Pg(main_2_pg), .Cin(clu4_1_c2), .Gg(main_2_gg));  // open: Cout
  lab4_1_main main_3 (
    .X(X[7:4]), .F(S[7:4]), .Y(Y[7:4]), .Pg(main_3_pg), .Cin(clu4_1_c1), .Gg(main_3_gg));  // open: Cout
  lab4_1_main main_4 (.X(X[3:0]), .F(S[3:0]), .Y(Y[3:0]), .Pg(main_4_pg), .Cin(C0), .Gg(main_4_gg));  // open: Cout
  // Probe on X
  // Probe on Y
  // Probe on S

  // Other names for the same wires on the sheet: S0[3:0] = S[3:0]; S1[3:0] = S[7:4]; S2[3:0] = S[11:8];
  //   S3[3:0] = S[15:12]

  // Notes on the sheet:
  //   Y: pull=down
  //   X: pull=down
  //   C0: pull=down
  //   输入引脚区
  //   请勿修改引脚名称、电路名称及电路封装外观
  //   提示：使用4位先行进位加法器和CLU子电路实现16位并行加法器
  //   功能说明:16位Adder  S=X+Y，C16为最高位进位位，C0为进位输入， Pg、Gg为成组进位生成传递函数
  //   输出引脚区
  //   +
  //   =
  //   无符号加法
endmodule
