// Logisim project lab4.3.circ as structural Verilog: 1 circuit, main circuit main
// 加法器
module main (
  input  Cin,
  input  [31:0] X,
  input  [31:0] Y,
  output OF,
  output Cout,
  output CF,
  output ZF,
  output [31:0] S,
  output SF
);

  wire and_1_out, and_2_out, main_1_pg, main_2_c16;

  lab4_2_main main_1 (
    .X(X[31:16]), .Y(Y[31:16]), .C0(main_2_c16), .S(S[31:16]), .C16(Cout), .Pg(main_1_pg), .Gg(main_1_pg));
  lab4_2_main main_2 (
    .X(X[15:0]), .Y(Y[15:0]), .C0(Cin), .S(S[15:0]), .C16(main_2_c16), .Pg(main_1_pg), .Gg(main_1_pg));
  xor xor_1 (CF, Cin, Cout);
  // Probe on X
  // Probe on Y
  // Probe on S
  Comparator #(.width(32), .mode("unsigned")) comparator_1 (.a(S), .b({32{1'b0}}), .eq(ZF));  // open: gt, lt
  and and_1 (and_1_out, X[31], Y[31], ~S[31]);  // AND_Gate
  and and_2 (and_2_out, ~X[31], ~Y[31], S[31]);  // AND_Gate
  or or_1 (OF, and_1_out, and_2_out);

  assign SF = S[31];
  // also tied to GND on the sheet: main_1_pg

  // Notes on the sheet:
  //   X: pull=down
  //   Cin: pull=down
  //   Y: pull=down
  //   输入引脚区
  //   输出引脚区
  //   请勿修改引脚名称、电路名称及电路封装外观
  //   提示：使用两个16位并行加法器子电路串行实现32位快速加法器
  //   功能说明:32位Adder  S=X+Y，Cout为最高位进位位，Cin为进位输入， S为和，溢出OF、进位CF、零ZF、符号SF。
  //   +
  //   =
  //   无符号加法
endmodule
