// Logisim project lab4.circ as structural Verilog: 9 circuits, main circuit main
module main (
);
endmodule

// CLU
module \_4位先行进位部件CLU  (
  input  P0,
  input  P1,
  input  P2,
  input  P3,
  input  G0,
  input  G1,
  input  G2,
  input  G3,
  input  C0,
  output C1,
  output C3,
  output C2,
  output C4,
  output Pg,
  output Gg
);

  wire and_1_out, and_2_out, and_3_out, and_4_out, and_5_out, and_6_out, and_7_out, and_8_out, and_9_out,
       and_10_out;

  and and_1 (and_1_out, C0, P0);
  and and_2 (and_2_out, C0, P0, P1);
  and and_3 (and_3_out, G0, P1);
  and and_4 (and_4_out, C0, P0, P1, P2);
  and and_5 (and_5_out, G0, P1, P2);
  and and_6 (and_6_out, G1, P2);
  and and_7 (and_7_out, C0, P0, P1, P2, P3);
  and and_8 (and_8_out, G0, P1, P2, P3);
  and and_9 (and_9_out, G1, P2, P3);
  and and_10 (and_10_out, G2, P3);
  or or_1 (C1, and_1_out, G0);
  or or_2 (C2, and_2_out, and_3_out, G1);
  or or_3 (C3, and_4_out, and_5_out, and_6_out, G2);
  or or_4 (C4, and_7_out, and_8_out, and_9_out, and_10_out, G3);
  and and_11 (Pg, P0, P1, P2, P3);
  or or_5 (Gg, and_8_out, and_9_out, and_10_out, G3);

  // Notes on the sheet:
  //   输入引脚
  //   四位先行进位逻辑单元CLU，C0为进位输入， C1C2C3C4为进位输出，Pg、Gg为成组进位生成传递函数
  //   输出引脚
endmodule

module FA (
  input  A,
  input  B,
  input  Cin,
  output F,
  output P,
  output G
);

  xor xor_1 (F, A, B, Cin);
  and and_1 (G, A, B);
  or or_1 (P, A, B);

  // Notes on the sheet:
  //   全加器
endmodule

module \_4位快速加法器CLA  (
  input  [3:0] X,
  input  [3:0] Y,
  input  Cin,
  output [3:0] F,
  output Cout,
  output Pg,
  output Gg
);

  wire fa_1_g, fa_1_p, \n4位先行进位部件clu_1_c1 , \n4位先行进位部件clu_1_c2 , \n4位先行进位部件clu_1_c3 , \全加器_2_g , \全加器_2_p ,
       \全加器_3_g , \全加器_3_p , \全加器_g , \全加器_p ;

  FA \u_全加器  (.A(X[3]), .F(F[3]), .B(Y[3]), .P(\全加器_p ), .Cin(\n4位先行进位部件clu_1_c3 ), .G(\全加器_g ));
  Hex_Digit_Display hex_digit_display_1 (.value(X));  // open: dp
  FA \u_全加器_2  (.A(X[2]), .F(F[2]), .B(Y[2]), .P(\全加器_2_p ), .Cin(\n4位先行进位部件clu_1_c2 ), .G(\全加器_2_g ));
  Hex_Digit_Display hex_digit_display_2 (.value(Y));  // open: dp
  \_4位先行进位部件CLU  \u_4位先行进位部件clu_1  (
    .P0(\全加器_3_p ), .P1(fa_1_p), .P2(\全加器_2_p ), .P3(\全加器_p ), .C1(\n4位先行进位部件clu_1_c1 ),
    .C3(\n4位先行进位部件clu_1_c3 ), .G0(\全加器_3_g ), .G1(fa_1_g), .G2(\全加器_2_g ), .G3(\全加器_g ),
    .C2(\n4位先行进位部件clu_1_c2 ), .C4(Cout), .C0(Cin), .Pg(Pg), .Gg(Gg));
  FA fa_1 (.A(X[1]), .F(F[1]), .B(Y[1]), .P(fa_1_p), .Cin(\n4位先行进位部件clu_1_c1 ), .G(fa_1_g));
  Hex_Digit_Display hex_digit_display_3 (.value(F));  // open: dp
  FA \u_全加器_3  (.A(X[0]), .F(F[0]), .B(Y[0]), .P(\全加器_3_p ), .Cin(Cin), .G(\全加器_3_g ));

  // Other names for the same wires on the sheet: Z[3:0] = F

  // Notes on the sheet:
  //   四位快速加法器CLA
  //   +
  //   =
  //   输出
  //   输入
endmodule

// 16-CLA
module \_16位先行进位加法器  (
  input  C0,
  input  [15:0] X,
  input  [15:0] Y,
  output C16,
  output Pg,
  output Gg,
  output [15:0] S
);

  wire \_4位CLA_2_gg , \_4位CLA_2_pg , \_4位CLA_3_gg , \_4位CLA_3_pg , \_4位CLA_4_gg , \_4位CLA_4_pg , \_4位CLA_gg ,
       \_4位CLA_pg , \n4位先行进位部件clu_1_c1 , \n4位先行进位部件clu_1_c2 , \n4位先行进位部件clu_1_c3 ;

  \_4位快速加法器CLA  \_4位CLA  (
    .X(X[15:12]), .F(S[15:12]), .Cout(C16), .Y(Y[15:12]), .Pg(\_4位CLA_pg ), .Cin(\n4位先行进位部件clu_1_c3 ),
    .Gg(\_4位CLA_gg ));
  \_4位快速加法器CLA  \_4位CLA_2  (
    .X(X[11:8]), .F(S[11:8]), .Y(Y[11:8]), .Pg(\_4位CLA_2_pg ), .Cin(\n4位先行进位部件clu_1_c2 ), .Gg(\_4位CLA_2_gg ));  // open: Cout
  \_4位先行进位部件CLU  \u_4位先行进位部件clu_1  (
    .P0(\_4位CLA_4_pg ), .P1(\_4位CLA_3_pg ), .P2(\_4位CLA_2_pg ), .P3(\_4位CLA_pg ), .C1(\n4位先行进位部件clu_1_c1 ),
    .C3(\n4位先行进位部件clu_1_c3 ), .G0(\_4位CLA_4_gg ), .G1(\_4位CLA_3_gg ), .G2(\_4位CLA_2_gg ), .G3(\_4位CLA_gg ),
    .C2(\n4位先行进位部件clu_1_c2 ), .C0(C0), .Pg(Pg), .Gg(Gg));  // open: C4
  \_4位快速加法器CLA  \_4位CLA_3  (
    .X(X[7:4]), .F(S[7:4]), .Y(Y[7:4]), .Pg(\_4位CLA_3_pg ), .Cin(\n4位先行进位部件clu_1_c1 ), .Gg(\_4位CLA_3_gg ));  // open: Cout
  \_4位快速加法器CLA  \_4位CLA_4  (
    .X(X[3:0]), .F(S[3:0]), .Y(Y[3:0]), .Pg(\_4位CLA_4_pg ), .Cin(C0), .Gg(\_4位CLA_4_gg ));  // open: Cout
  // Probe on X
  // Probe on Y
  // Probe on S

  // Other names for the same wires on the sheet: S0[3:0] = S[3:0]; S1[3:0] = S[7:4]; S2[3:0] = S[11:8];
  //   S3[3:0] = S[15:12]

  // Notes on the sheet:
  //   Y: pull=down
  //   X: pull=down
  //   C0: pull=down
  //   16位快速加法器
  //   输入引脚区
  //   功能说明:16位Adder  S=X+Y，C16为最高位进位位，C0为进位输入， Pg、Gg为成组进位生成传递函数
  //   输出引脚区
  //   +
  //   =
  //   无符号加法
endmodule

// 加法器
module \_32位加法器  (
  input  [31:0] X,
  input  Cin,
  input  [31:0] Y,
  output OF,
  output CF,
  output [31:0] S,
  output ZF,
  output SF,
  output Cout
);

  wire and_1_out, and_2_out, \n16位先行进位加法器_1_pg , \n16位先行进位加法器_2_c16 ;

  \_16位先行进位加法器  \u_16位先行进位加法器_1  (
    .X(X[31:16]), .Y(Y[31:16]), .C0(\n16位先行进位加法器_2_c16 ), .S(S[31:16]), .C16(Cout), .Pg(\n16位先行进位加法器_1_pg ),
    .Gg(\n16位先行进位加法器_1_pg ));
  \_16位先行进位加法器  \u_16位先行进位加法器_2  (
    .X(X[15:0]), .Y(Y[15:0]), .C0(Cin), .S(S[15:0]), .C16(\n16位先行进位加法器_2_c16 ), .Pg(\n16位先行进位加法器_1_pg ),
    .Gg(\n16位先行进位加法器_1_pg ));
  xor xor_1 (CF, Cin, Cout);
  Comparator #(.width(32), .mode("unsigned")) comparator_1 (.a(S), .b({32{1'b0}}), .eq(ZF));  // open: gt, lt
  // Probe on X
  // Probe on Y
  // Probe on S
  and and_1 (and_1_out, X[31], Y[31], ~S[31]);  // AND_Gate
  or or_1 (OF, and_1_out, and_2_out);
  and and_2 (and_2_out, ~X[31], ~Y[31], S[31]);  // AND_Gate

  assign SF = S[31];
  // also tied to GND on the sheet: \n16位先行进位加法器_1_pg 

  // Notes on the sheet:
  //   Cin: pull=down
  //   Y: pull=down
  //   X: pull=down
  //   带标志位的32位快速加法器
  //   输入引脚区
  //   输出引脚区
  //   功能说明:32位Adder  S=X+Y，Cout为最高位进位位，Cin为进位输入， S为和，OF、CF、ZF、SF为标志位。
  //   +
  //   =
  //   无符号加法
endmodule

// ALU操作控制信号
module \ALU操作控制信号生成部件  (
  input  [3:0] ALUctr,
  output SUBctr,
  output SFTctr,
  output SIGctr,
  output ALctr,
  output [2:0] OPctr
);

  wire and_2_out, and_3_out, and_6_out, and_7_out, and_8_out, and_9_out, and_10_out, and_11_out, and_12_out;

  and and_1 (SIGctr, ~ALUctr[0], ALUctr[1], ~ALUctr[2], ~ALUctr[3]);  // AND_Gate
  and and_2 (and_2_out, ALUctr[1], ~ALUctr[2], ~ALUctr[3]);  // AND_Gate
  and and_3 (and_3_out, ~ALUctr[0], ~ALUctr[1], ~ALUctr[2], ALUctr[3]);  // AND_Gate
  and and_4 (SFTctr, ALUctr[0], ~ALUctr[1], ~ALUctr[2], ~ALUctr[3]);  // AND_Gate
  and and_5 (ALctr, ALUctr[0], ~ALUctr[1], ALUctr[2], ALUctr[3]);  // AND_Gate
  and and_6 (and_6_out, ALUctr[1], ~ALUctr[2], ~ALUctr[3]);  // AND_Gate
  and and_7 (and_7_out, ALUctr[0], ~ALUctr[1], ~ALUctr[3]);  // AND_Gate
  and and_8 (and_8_out, ALUctr[0], ALUctr[2], ALUctr[3]);
  and and_9 (and_9_out, ALUctr[1], ~ALUctr[2], ~ALUctr[3]);  // AND_Gate
  and and_10 (and_10_out, ~ALUctr[0], ALUctr[2], ~ALUctr[3]);  // AND_Gate
  and and_11 (and_11_out, ALUctr[0], ALUctr[1], ALUctr[2]);
  and and_12 (and_12_out, ~ALUctr[0], ~ALUctr[1], ALUctr[2], ~ALUctr[3]);  // AND_Gate
  or or_1 (SUBctr, and_2_out, and_3_out);
  or or_2 (OPctr[2], and_6_out, and_7_out, and_8_out);
  or or_3 (OPctr[1], and_9_out, and_10_out);
  or or_4 (OPctr[0], and_11_out, and_12_out);

  // Other names for the same wires on the sheet: LRctr = SFTctr

  // Notes on the sheet:
  //   输入引脚
  //   ALU操作控制信号生成部件
  //   输出引脚
endmodule

module ALU (
  input  [31:0] A,
  input  [31:0] B,
  input  [3:0] ALUctr,
  output [31:0] S,
  output Zero
);

  wire \alu操作控制信号生成部件_1_alctr , \alu操作控制信号生成部件_1_sftctr , \alu操作控制信号生成部件_1_sigctr , \alu操作控制信号生成部件_1_subctr ,
       multiplexer_1_out, \n32位加法器_1_cout , \n32位加法器_1_of , \n32位加法器_1_sf , xor_3_out, xor_4_out;
  wire [2:0] \alu操作控制信号生成部件_1_opctr ;
  wire [31:0] and_1_out, bit_extender_1_out, bit_extender_2_out, \n32位加法器_1_s , \n32位桶形移位器_1_dataout ,
       or_1_out, xor_1_out, xor_2_out;

  assign xor_1_out = B ^ bit_extender_1_out;  // XOR_Gate xor_1, 32 bits wide
  assign bit_extender_1_out = {{31{\alu操作控制信号生成部件_1_subctr }}, \alu操作控制信号生成部件_1_subctr };  // Bit_Extender bit_extender_1
  assign and_1_out = A & B;  // AND_Gate and_1, 32 bits wide
  assign or_1_out = A | B;  // OR_Gate or_1, 32 bits wide
  assign xor_2_out = A ^ B;  // XOR_Gate xor_2, 32 bits wide
  \_32位桶形移位器  \u_32位桶形移位器_1  (
    .L_R(\alu操作控制信号生成部件_1_sftctr ), .shamt(B[4:0]), .DataIn(A), .DataOut(\n32位桶形移位器_1_dataout ),
    .A_L(\alu操作控制信号生成部件_1_alctr ));
  \_32位加法器  \u_32位加法器_1  (
    .Cin(\alu操作控制信号生成部件_1_subctr ), .Cout(\n32位加法器_1_cout ), .X(A), .Y(xor_1_out), .S(\n32位加法器_1_s ),
    .OF(\n32位加法器_1_of ), .ZF(Zero), .SF(\n32位加法器_1_sf ));  // open: CF
  xor xor_3 (xor_3_out, \alu操作控制信号生成部件_1_subctr , \n32位加法器_1_cout );
  Multiplexer #(.enable("false")) multiplexer_1 (
    .in0(xor_3_out), .in1(xor_4_out), .out(multiplexer_1_out), .sel(\alu操作控制信号生成部件_1_sigctr ));
  xor xor_4 (xor_4_out, \n32位加法器_1_of , \n32位加法器_1_sf );
  Multiplexer #(.select(3), .width(32), .enable("false")) multiplexer_2 (
    .in0(\n32位加法器_1_s ), .in1(and_1_out), .in2(or_1_out), .in3(xor_2_out), .in4(\n32位桶形移位器_1_dataout ),
    .in5(B), .in6(bit_extender_2_out), .out(S), .sel(\alu操作控制信号生成部件_1_opctr ));  // open: in7
  \ALU操作控制信号生成部件  \alu操作控制信号生成部件_1  (
    .ALUctr(ALUctr), .SUBctr(\alu操作控制信号生成部件_1_subctr ), .SFTctr(\alu操作控制信号生成部件_1_sftctr ),
    .SIGctr(\alu操作控制信号生成部件_1_sigctr ), .ALctr(\alu操作控制信号生成部件_1_alctr ), .OPctr(\alu操作控制信号生成部件_1_opctr ));
  assign bit_extender_2_out = {{31{1'b0}}, multiplexer_1_out};  // Bit_Extender bit_extender_2
  // Probe on A
  // Probe on B
  // Probe on S

  // Other names for the same wires on the sheet: Result[31:0] = S

  // Notes on the sheet:
  //   B: pull=down
  //   A: pull=down
  //   ALUctr: pull=down
  //   输入引脚区
  //   32位算术逻辑运算单元ALU
  //   功能说明:32位ALU，输入32位操作数A、B，4位控制信号ALUctr，输出32位结果Reseult和1位Zero标志位
  //   输出引脚区
  //   操作数和结果
endmodule

// 移位器
module \_32位桶形移位器  (
  input  L_R,
  input  [4:0] shamt,
  input  [31:0] DataIn,
  input  A_L,
  output [31:0] DataOut
);

  wire [3:0] multiplexer_4_out, multiplexer_4_out_2;
  wire [23:0] multiplexer_4_out_3;
  wire [31:0] multiplexer_1_out, multiplexer_2_out, multiplexer_3_out, multiplexer_5_out, multiplexer_6_out,
       multiplexer_7_out, multiplexer_8_out, multiplexer_10_out;

  Multiplexer #(.width(32), .enable("false")) multiplexer_1 (
    .in0(DataIn), .in1(multiplexer_2_out), .out(multiplexer_1_out), .sel(shamt[0]));
  Multiplexer #(.select(2), .width(32), .enable("false")) multiplexer_2 (
    .in0({1'b0, DataIn[31:1]}), .in1({{2{DataIn[31]}}, DataIn[30:1]}), .in2({DataIn[30:0], 1'b0}),
    .in3({DataIn[30:0], DataIn[31]}), .out(multiplexer_2_out), .sel({L_R, A_L}));
  Multiplexer #(.select(2), .width(32), .enable("false")) multiplexer_3 (
    .in0({2'b00, multiplexer_1_out[31:2]}), .in1({{3{multiplexer_1_out[31]}}, multiplexer_1_out[30:2]}),
    .in2({multiplexer_1_out[29:0], 2'b00}), .in3({multiplexer_1_out[29:0], multiplexer_1_out[31:30]}),
    .out(multiplexer_3_out), .sel({L_R, A_L}));
  Multiplexer #(.width(32), .enable("false")) multiplexer_4 (
    .in0(multiplexer_1_out), .in1(multiplexer_3_out),
    .out({multiplexer_4_out, multiplexer_4_out_3, multiplexer_4_out_2}), .sel(shamt[1]));
  Multiplexer #(.width(32), .enable("false")) multiplexer_5 (
    .in0({multiplexer_4_out, multiplexer_4_out_3, multiplexer_4_out_2}), .in1(multiplexer_6_out),
    .out(multiplexer_5_out), .sel(shamt[2]));
  Multiplexer #(.select(2), .width(32), .enable("false")) multiplexer_6 (
    .in0({4'b0000, multiplexer_4_out, multiplexer_4_out_3}),
    .in1({{5{multiplexer_4_out[3]}}, multiplexer_4_out[2:0], multiplexer_4_out_3}),
    .in2({multiplexer_4_out_3, multiplexer_4_out_2, 4'b0000}),
    .in3({multiplexer_4_out_3, multiplexer_4_out_2, multiplexer_4_out}), .out(multiplexer_6_out),
    .sel({L_R, A_L}));
  Multiplexer #(.width(32), .enable("false")) multiplexer_7 (
    .in0(multiplexer_5_out), .in1(multiplexer_8_out), .out(multiplexer_7_out), .sel(shamt[3]));
  Multiplexer #(.select(2), .width(32), .enable("false")) multiplexer_8 (
    .in0({{8{1'b0}}, multiplexer_5_out[31:8]}), .in1({{9{multiplexer_5_out[31]}}, multiplexer_5_out[30:8]}),
    .in2({multiplexer_5_out[23:0], {8{1'b0}}}), .in3({multiplexer_5_out[23:0], multiplexer_5_out[31:24]}),
    .out(multiplexer_8_out), .sel({L_R, A_L}));
  Multiplexer #(.width(32), .enable("false")) multiplexer_9 (
    .in0(multiplexer_7_out), .in1(multiplexer_10_out), .out(DataOut), .sel(shamt[4]));
  Multiplexer #(.select(2), .width(32), .enable("false")) multiplexer_10 (
    .in0({{16{1'b0}}, multiplexer_7_out[31:16]}),
    .in1({{17{multiplexer_7_out[31]}}, multiplexer_7_out[30:16]}),
    .in2({multiplexer_7_out[15:0], {16{1'b0}}}), .in3({multiplexer_7_out[15:0], multiplexer_7_out[31:16]}),
    .out(multiplexer_10_out), .sel({L_R, A_L}));

  // Other names for the same wires on the sheet: Din[31:0] = DataIn; Arth_Logic = A_L; Left_Right = L_R;
  //   Dout[31:0] = DataOut

  // Notes on the sheet:
  //   输入信号
  //   L/R=1左移；=0右移
  //   A/L=1算术右移；=0逻辑右移
  //   32位桶形移位器
  //   输出信号
endmodule
